# Fritzing sketch Schematic (saved by Fritzing 0.8.7b)

parts:
  Part1 = 2.4 Touchscreen TFT Breakout w:MicroSD
  Part2 = Arduino Nano (Rev3.0)
  Part3 = Arduino Nano (Rev3.0)
  U1 = Vibration Motor- ROB-08449 [package=vibe-motor-10mm]
  DS4 = DS18B20 1-Wire Temperature Sensor Probe Cable
  R1 = Resistor [package="2010 [SMD]"]
  R2 = Resistor [package="2010 [SMD]"]
  Q1 = TRANSISTOR_NPN [package=to-92-ammo]
  J1 = Power Jack [package=power_jack_combo]
  M8 = DC Motor
  D4 = Diode [package=diode-1n4001]
  R3 = Resistor [package="2010 [SMD]"]
  M9 = DC Motor
  D5 = Diode [package=diode-1n4001]
  R4 = Resistor [package="2010 [SMD]"]
  M10 = DC Motor
  Q3 = TRANSISTOR_NPN [package=to-92-ammo]
  D6 = Diode [package=diode-1n4001]
  R5 = Resistor [package="2010 [SMD]"]
  M11 = DC Motor
  Q4 = TRANSISTOR_NPN [package=to-92-ammo]
  D7 = Diode [package=diode-1n4001]
  M12 = DC Motor
  Q5 = TRANSISTOR_NPN [package=to-92-ammo]
  D8 = Diode [package=diode-1n4001]
  R7 = Resistor [package="2010 [SMD]"]
  M13 = DC Motor
  Q6 = TRANSISTOR_NPN [package=to-92-ammo]
  D9 = Diode [package=diode-1n4001]
  R8 = Resistor [package="2010 [SMD]"]
  M14 = DC Motor
  Q7 = TRANSISTOR_NPN [package=to-92-ammo]
  D10 = Diode [package=diode-1n4001]
  R6 = Resistor [package="2010 [SMD]"]
  J2 = Screw terminal - 2 pins [package=THT]
  Q8 = Basic FET N-Channel [package="TO220 [THT]"]
  Q9 = TRANSISTOR_NPN [package=to-92-ammo]
  Q2 = TRANSISTOR_NPN [package=to-92-ammo]
  Q10 = TRANSISTOR_NPN [package=to-92-ammo]
  Q11 = TRANSISTOR_NPN [package=to-92-ammo]
  Q12 = TRANSISTOR_NPN [package=to-92-ammo]
  Q13 = TRANSISTOR_NPN [package=to-92-ammo]
  R10 = Resistor [package="2010 [SMD]"]  # not connected
  R9 = Resistor [package="2010 [SMD]"]  # not connected

nets:
  GND: Part1.GND, Part2.GND, Part3.GND, U1.+, DS4.GND, DS4.shield, Q1.C, J1.GND, J1.GNDBREAK, Q3.C, Q4.C, Q5.C, Q6.C, Q7.C, Q8.source, Q9.C, Q11.C, Q12.C, Q13.C
  VIN: Part1.VIN, Part2.5V
  N1: Part1.CS, Part2.A3
  N2: Part1.C/D, Part2.A2
  N3: Part1.WR, Part2.A1
  N4: Part1.RD, Part2.A0
  N5: Part1.RST, Part2.RESET
  N6: Part1.D0, Part2.D8
  N7: Part1.D1, Part2.D9
  N8: Part1.D2, Part2.D2
  N9: Part1.D3, Part2.D3
  N10: Part1.D4, Part2.D4
  N11: Part1.D5, Part2.D5
  N12: Part1.D6, Part2.D6
  N13: Part1.D7, Part2.D7
  N14: Part2.D12/MISO, Part3.D2
  VIN_2: Part2.VIN, Part3.VIN, J1.PWR, M8.pin_1, D4.A, M9.pin_1, D5.A, M10.pin_1, D6.A, M11.pin_1, D7.A, M12.pin_1, D8.A, M13.pin_1, D9.A, M14.pin_1, D10.A, J2.pin1
  N15: Part2.A5, Part3.A5
  N16: Part2.A4, Part3.A4
  N17: Part3.D3, U1.-
  N18: Part3.D4, R8.Pin_0
  N19: Part3.D5, R7.Pin_0
  N20: Part3.D6, Q8.gate
  N21: Part3.D7, DS4.DQ, R2.Pin_1
  N22: Part3.D8, R6.Pin_0
  5V: Part3.5V, DS4.VDD, R2.Pin_0
  N23: Part3.A3, R1.Pin_0
  N24: Part3.A2, R3.Pin_0
  N25: Part3.A1, R4.Pin_0
  N26: Part3.A0, R5.Pin_0
  N27: R1.Pin_1, Q1.E, Q9.E
  N28: Q1.B, M8.pin_2, D4.C, Q9.B
  N29: R3.Pin_1, Q2.E, Q10.E
  N30: M9.pin_2, D5.C, Q2.B, Q10.B
  N31: R4.Pin_1, Q3.E, Q11.E
  N32: M10.pin_2, Q3.B, D6.C, Q11.B
  N33: R5.Pin_1, Q4.E, Q12.E
  N34: M11.pin_2, Q4.B, D7.C, Q12.B
  N35: M12.pin_2, Q5.B, D8.C, Q13.B
  N36: Q5.E, R6.Pin_1, Q13.E
  N37: R7.Pin_1, Q6.E
  N38: M13.pin_2, Q6.B, D9.C
  N39: R8.Pin_1, Q7.E
  N40: M14.pin_2, Q7.B, D10.C
  N41: J2.pin2, Q8.drain
  N42: Q2.C, Q10.C

notes:
  To heater
  2N3904

custom parts:
  2.4 Touchscreen TFT Breakout w:MicroSD: Add some jazz & pizzazz to your project with a color touchscreen LCD. This TFT display is 2.4" diagonal with a bright (4 white-LED) backlight and it's colorful! 240x320 pixels with individual RGB pixel control, this has way more resolution than a black and white 128x64 display. As a bonus, this display has a resistive touchscreen attached to it already, so you can detect finger presses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
